# Fritzing sketch BME280 (saved by Fritzing 0.9.10b)
breadboards: 1

parts:
  V1 = DC Power [voltage=5]
  Mod1 = Amica NodeMCU DEVKIT 1.0
  Part1 = BME280 Breakout  # not connected

nets:
  N1: V1.V-, Mod1.pin2, Mod1.pin_9
  N2: Mod1.pin1, Mod1.pin_10
